# Fritzing sketch K2000 (saved by Fritzing 0.9.9b)
breadboards: 1

parts:
  LED1 = LED - 5mm [color="Red (633nm)" current=0.030 package="5 mm [THT]"]
  LED2 = LED - 5mm [color="Red (633nm)" current=0.030 package="5 mm [THT]"]
  LED3 = LED - 5mm [color="Red (633nm)" current=0.030 package="5 mm [THT]"]
  LED4 = LED - 5mm [color="Red (633nm)" current=0.030 package="5 mm [THT]"]
  LED5 = LED - 5mm [color="Red (633nm)" current=0.030 package="5 mm [THT]"]
  LED6 = LED - 5mm [color="Red (633nm)" current=0.030 package="5 mm [THT]"]
  R1 = Resistor [tolerance=±5% power=0.25 resistance=220 package=THT]
  R2 = Resistor [tolerance=±5% power=0.25 resistance=220 package=THT]
  R3 = Resistor [tolerance=±5% power=0.25 resistance=220 package=THT]
  R4 = Resistor [tolerance=±5% power=0.25 resistance=220 package=THT]
  R5 = Resistor [tolerance=±5% power=0.25 resistance=220 package=THT]
  R6 = Resistor [tolerance=±5% power=0.25 resistance=220 package=THT]
  Part1 = Arduino Uno (Rev3)

nets:
  N1: LED1.cathode, R1.Pin_0
  N2: LED1.anode, Part1.D11_PWM/MOSI
  N3: LED2.cathode, R2.Pin_0
  N4: LED2.anode, Part1.D10_PWM/SS
  N5: LED3.cathode, R3.Pin_0
  N6: LED3.anode, Part1.D9_PWM
  N7: LED4.cathode, R4.Pin_0
  N8: LED4.anode, Part1.D6_PWM
  N9: LED5.cathode, R5.Pin_0
  N10: LED5.anode, Part1.D5_PWM
  N11: LED6.cathode, R6.Pin_0
  N12: LED6.anode, Part1.D3_PWM
  N13: R1.Pin_1, R2.Pin_1, R3.Pin_1, R4.Pin_1, R5.Pin_1, R6.Pin_1, Part1.GND
