# Fritzing sketch TrafficLight (saved by Fritzing 0.9.9b)
breadboards: 1

parts:
  LED2 = LED - 5mm [color="Yellow (585nm)" current=0.030 package="5 mm [THT]"]
  LED3 = LED - 5mm [color="Green (555nm)" current=0.030 package="5 mm [THT]"]
  Part1 = Arduino Uno (Rev3)
  LED1 = LED - 5mm [color="Red (633nm)" current=0.030 package="5 mm [THT]"]
  R1 = Resistor [tolerance=±5% power=0.25 resistance=220 package=THT]
  R3 = Resistor [tolerance=±5% power=0.25 resistance=220 package=THT]
  R4 = Resistor [tolerance=±5% power=0.25 resistance=220 package=THT]

nets:
  N1: LED2.cathode, R3.Pin_0
  N2: LED2.anode, Part1.D9_PWM
  N3: LED3.cathode, R4.Pin_0
  N4: LED3.anode, Part1.D8
  N5: Part1.D10_PWM/SS, LED1.anode
  N6: Part1.GND, R1.Pin_1, R3.Pin_1, R4.Pin_1
  N7: LED1.cathode, R1.Pin_0
